// Digital circuit 8-Bit Cumulative Adder.dig as structural Verilog
module _8_Bit_Cumulative_Adder (
  input  [7:0] A,
  input  Clr,
  output [7:0] Sum
);

  wire Add_out;
  wire [7:0] _8_bit_adder_1_s;

  Button Add (.out(Add_out));
  _8_Bit_Adder _8_bit_adder_1 (.CI(1'b0), .A(A), .B(Sum), .S(_8_bit_adder_1_s));  // open: CO
  _8_Bit_Latch_Edge_Triggered_Clearable _8_bit_latch_edge_triggered_clearable_1 (
    .D(_8_bit_adder_1_s), .Clk(Add_out), .Clr(Clr), .Q(Sum));
endmodule
