// Digital circuit D Flip-Flop.dig as structural Verilog
module D_Flip_Flop (
  input  Data,
  input  Clock,
  output Q,
  output Q_2
);

  wire and_1_out, and_2_out, not_1_out;

  not not_1 (not_1_out, Data);
  and and_1 (and_1_out, not_1_out, Clock);
  and and_2 (and_2_out, Data, Clock);
  R_S_Flip_Flop r_s_flip_flop_1 (.R(and_1_out), .S(and_2_out), .Q(Q), .Q_2(Q_2));
endmodule
